// Logisim project Projeto 1 - Circuitos Digitais.circ as structural Verilog: 1 circuit, main circuit main
module main (
  input  A,
  input  B,
  input  C,
  input  D,
  input  E,
  input  F,
  input  G
);

  wire a_2_out, a_3_out, a_out, and_1_out, and_2_out, and_3_out, and_4_out, and_5_out, and_6_out, and_7_out,
       and_8_out, and_9_out, and_10_out, and_11_out, and_12_out, and_13_out, and_14_out, and_15_out,
       and_16_out, and_17_out, and_18_out, and_19_out, and_20_out, and_21_out, and_22_out, and_23_out,
       and_24_out, and_25_out, and_26_out, and_27_out, and_28_out, and_29_out, and_30_out, and_31_out,
       and_32_out, and_33_out, and_34_out, and_35_out, and_36_out, and_37_out, and_38_out, and_39_out,
       and_40_out, and_41_out, and_42_out, and_43_out, and_44_out, and_45_out, and_46_out, and_47_out,
       and_48_out, and_49_out, and_50_out, and_51_out, and_52_out, and_53_out, and_54_out, and_55_out,
       and_56_out, and_57_out, and_58_out, and_59_out, and_60_out, and_61_out, and_62_out, and_63_out,
       and_64_out, and_65_out, and_66_out, and_67_out, and_68_out, and_69_out, and_70_out, and_71_out,
       and_72_out, and_73_out, and_74_out, and_75_out, and_76_out, and_77_out, and_78_out, and_79_out,
       b_2_out, b_3_out, b_out, c_2_out, c_3_out, c_out, d_2_out, d_3_out, d_out, e_2_out, e_3_out, e_out,
       f_2_out, f_3_out, f_out, g_2_out, g_3_out, g_out, Letras_out, Num_out, or_1_out, or_2_out, or_3_out,
       or_4_out, or_5_out, or_6_out, or_7_out;

  and and_1 (and_1_out, Letras_out, a_out);
  and and_2 (and_2_out, Letras_out, b_out);
  and and_3 (and_3_out, Letras_out, c_out);
  and and_4 (and_4_out, Letras_out, d_out);
  and and_5 (and_5_out, Letras_out, e_out);
  and and_6 (and_6_out, Letras_out, f_out);
  and and_7 (and_7_out, Letras_out, g_out);
  and and_8 (and_8_out, Letras_out, ~D, E, ~F);  // AND_Gate
  and Letras (Letras_out, ~C, ~B, A);  // AND_Gate
  or u_a (a_out, and_10_out, and_11_out, and_12_out);
  or u_b (b_out, and_27_out, and_28_out);
  or u_c (c_out, and_13_out, and_14_out, and_15_out);
  or u_d (d_out, and_29_out, and_30_out);
  or u_e (e_out, and_16_out, and_17_out, and_18_out, and_19_out);
  or u_f (f_out, and_20_out, and_21_out, and_22_out);
  or u_g (g_out, and_23_out, and_24_out, and_25_out);
  and and_9 (and_9_out, Letras_out, ~D, ~E, G);  // AND_Gate
  or or_1 (or_1_out, and_8_out, and_9_out, and_26_out);
  and Num (Num_out, ~A, B, C);  // AND_Gate
  and and_10 (and_10_out, ~D, ~E, G);  // AND_Gate
  and and_11 (and_11_out, ~D, E, F, ~G);  // AND_Gate
  and and_12 (and_12_out, ~D, ~F, G);  // AND_Gate
  and and_13 (and_13_out, ~D, E, ~F, ~G);  // AND_Gate
  and and_14 (and_14_out, ~D, ~E, ~F, G);  // AND_Gate
  and and_15 (and_15_out, ~D, ~E, F, ~G);  // AND_Gate
  and and_16 (and_16_out, ~D, E, ~F);  // AND_Gate
  and and_17 (and_17_out, ~D, ~F, G);  // AND_Gate
  and and_18 (and_18_out, ~D, ~E, F);  // AND_Gate
  and and_19 (and_19_out, ~D, F, ~G);  // AND_Gate
  and and_20 (and_20_out, ~D, ~F, G);  // AND_Gate
  and and_21 (and_21_out, ~D, ~E, G);  // AND_Gate
  and and_22 (and_22_out, ~D, F, ~G);  // AND_Gate
  and and_23 (and_23_out, ~D, E, ~F);  // AND_Gate
  and and_24 (and_24_out, ~D, ~F, G);  // AND_Gate
  and and_25 (and_25_out, ~D, F, ~G);  // AND_Gate
  and and_26 (and_26_out, Letras_out, ~D, F, ~G);  // AND_Gate
  and and_27 (and_27_out, ~D, E, ~F, ~G);  // AND_Gate
  and and_28 (and_28_out, ~D, ~E, ~F, G);  // AND_Gate
  and and_29 (and_29_out, ~D, E, ~F);  // AND_Gate
  and and_30 (and_30_out, ~D, ~E, F);  // AND_Gate
  and and_31 (and_31_out, Letras_out, ~D, F, ~G);  // AND_Gate
  LED led_1 (.in(or_1_out));
  LED led_2 (.in(and_31_out));
  LED led_3 (.in(Num_out));
  and and_32 (and_32_out, ~D, E, ~G);  // AND_Gate
  and and_33 (and_33_out, ~D, E, ~F);  // AND_Gate
  and and_34 (and_34_out, D, ~E, ~F);  // AND_Gate
  and and_35 (and_35_out, ~D, ~F, ~G);  // AND_Gate
  and and_36 (and_36_out, ~D, E, ~F);  // AND_Gate
  and and_37 (and_37_out, D, ~E, ~F);  // AND_Gate
  and and_38 (and_38_out, ~D, ~E, F);  // AND_Gate
  and and_39 (and_39_out, ~D, F, ~G);  // AND_Gate
  LED led_4 (.in(or_3_out));
  LED led_5 (.in(or_2_out));
  LED led_6 (.in(Num_out));
  and and_40 (and_40_out, ~D, ~E, ~G);  // AND_Gate
  and and_41 (and_41_out, D, ~E, ~F);  // AND_Gate
  and and_42 (and_42_out, ~D, E, G);  // AND_Gate
  and and_43 (and_43_out, ~D, F);  // AND_Gate
  and and_44 (and_44_out, ~D, ~E);  // AND_Gate
  and and_45 (and_45_out, ~E, ~F);  // AND_Gate
  and and_46 (and_46_out, ~D, ~F, ~G);  // AND_Gate
  and and_47 (and_47_out, ~D, F, G);  // AND_Gate
  and and_48 (and_48_out, ~E, ~F);  // AND_Gate
  and and_49 (and_49_out, ~D, E);  // AND_Gate
  and and_50 (and_50_out, ~D, G);  // AND_Gate
  and and_51 (and_51_out, ~E, ~F, ~G);  // AND_Gate
  and and_52 (and_52_out, ~D, E, ~F, G);  // AND_Gate
  and and_53 (and_53_out, ~D, ~E, F);  // AND_Gate
  and and_54 (and_54_out, ~D, F, ~G);  // AND_Gate
  and and_55 (and_55_out, ~E, ~F, ~G);  // AND_Gate
  and and_56 (and_56_out, ~D, F, ~G);  // AND_Gate
  LED led_7 (.in(or_4_out));
  LED led_8 (.in(or_5_out));
  LED led_9 (.in(1'b0));
  or a_2 (a_2_out, and_40_out, and_41_out, and_42_out, and_43_out);
  or b_2 (b_2_out, and_44_out, and_45_out, and_46_out, and_47_out);
  or c_2 (c_2_out, and_48_out, and_49_out, and_50_out);
  or d_2 (d_2_out, and_51_out, and_52_out, and_53_out, and_54_out);
  or e_2 (e_2_out, and_55_out, and_56_out);
  or f_2 (f_2_out, and_32_out, and_33_out, and_34_out, and_35_out);
  or g_2 (g_2_out, and_36_out, and_37_out, and_38_out, and_39_out);
  LED led_10 (.in(or_7_out));
  LED led_11 (.in(or_6_out));
  LED led_12 (.in(1'b0));
  _7_Segment_Display u_7_segment_display_1 (
    .g(g_3_out), .f(f_3_out), .a(a_3_out), .b(b_3_out), .e(e_3_out), .d(d_3_out), .c(c_3_out), .dp(1'b0));
  and and_57 (and_57_out, Num_out, a_2_out);
  and and_58 (and_58_out, Num_out, b_2_out);
  and and_59 (and_59_out, Num_out, c_2_out);
  and and_60 (and_60_out, Num_out, d_2_out);
  and and_61 (and_61_out, Num_out, e_2_out);
  and and_62 (and_62_out, Num_out, f_2_out);
  and and_63 (and_63_out, Num_out, g_2_out);
  or or_2 (or_2_out, Num_out, and_64_out);
  and and_64 (and_64_out, Letras_out, ~D, E, ~F);  // AND_Gate
  or g_3 (g_3_out, and_63_out, and_7_out);
  or f_3 (f_3_out, and_62_out, and_6_out);
  or e_3 (e_3_out, and_61_out, and_5_out);
  or d_3 (d_3_out, and_60_out, and_4_out);
  or c_3 (c_3_out, and_59_out, and_3_out);
  or b_3 (b_3_out, and_58_out, and_2_out);
  or a_3 (a_3_out, and_57_out, and_1_out);
  and and_65 (and_65_out, Letras_out, ~D, E, ~G);  // AND_Gate
  and and_66 (and_66_out, Letras_out, ~D, ~E, F, G);  // AND_Gate
  or or_3 (or_3_out, Num_out, and_65_out, and_66_out);
  and and_67 (and_67_out, Num_out, ~D, E, ~F);  // AND_Gate
  and and_68 (and_68_out, Num_out, ~D, G);  // AND_Gate
  or or_4 (or_4_out, and_67_out, and_68_out, and_69_out, and_70_out);
  and and_69 (and_69_out, Num_out, ~D, F);  // AND_Gate
  and and_70 (and_70_out, Num_out, D, ~E, ~F, ~G);  // AND_Gate
  and and_71 (and_71_out, Num_out, ~E, ~F, ~G);  // AND_Gate
  and and_72 (and_72_out, Num_out, D, ~E, ~F);  // AND_Gate
  and and_73 (and_73_out, Num_out, ~D, E, F);  // AND_Gate
  or or_5 (or_5_out, and_71_out, and_72_out, and_73_out, and_74_out);
  and and_74 (and_74_out, Num_out, ~D, F, ~G);  // AND_Gate
  and and_75 (and_75_out, Num_out, ~E, ~F, ~G);  // AND_Gate
  and and_76 (and_76_out, Num_out, ~D, E);  // AND_Gate
  or or_6 (or_6_out, and_75_out, and_76_out);
  and and_77 (and_77_out, Num_out, ~D, ~F, ~G);  // AND_Gate
  and and_78 (and_78_out, Num_out, ~D, F, G);  // AND_Gate
  or or_7 (or_7_out, and_77_out, and_78_out, and_79_out);
  and and_79 (and_79_out, Num_out, D, ~E, ~F, G);  // AND_Gate

  // Notes on the sheet:
  //   o
  //   p
  //   q
  //   o
  //   t
  //   p
  //   s
  //   r
  //   q
  //   r
  //   u
  //   z
  //   v
  //   y
  //   x
  //   w
  //   f
  //   g
  //   e
  //   d
  //   s
  //   a
  //   b
  //   c
  //   t
  //   u
  //   v
  //   w / x
  //   y
  //   Z
endmodule
